// Digital circuit atk16.dig as structural Verilog
module atk16 (
  input  clk
);

  wire ALU_OE, and_1_out, FR_IE, HALT, IR9_OE, IR12_OE, IR_IE, MAR_IE, MEM_IE, MEM_OE, not_1_out, OP_PARITY,
       PC_CO, PC_IE, PC_OE, R1_OE, R2_OE, RW_IE, US_RS;
  wire [2:0] IR0, IR1, IR2, IR3;
  wire [3:0] ALU_flags, bitselector_2_out, FR_q, OPCODE;
  wire [14:0] demultiplexer_1_out_0, demultiplexer_1_out_1;
  wire [15:0] ALU_y, driver_1_out, driver_3_out, MAR_q, MEM_RAM_q, MEM_ROM_d, PC_out, Register_file_db;

  assign driver_1_out = IR9_OE ? {{7{1'b0}}, IR1, IR2, IR3} : 16'bz;  // Driver driver_1
  assign driver_1_out = IR12_OE ? {4'b0000, IR0, IR1, IR2, IR3} : 16'bz;  // Driver driver_2
  RegisterFile #(.AddrBits(3), .Bits(16)) Register_file (
    .Din(driver_1_out), .we(RW_IE), .Rw(IR2), .C(clk), .Ra(IR0), .Rb(IR1), .Da(driver_1_out),
    .Db(Register_file_db));
  CounterPreset #(.Bits(16), .isProgramCounter("true")) PC (
    .en(PC_CO), .C(clk), .dir(1'b0), .in(driver_3_out), .ld(IR_IE), .clr(1'b0), .out(PC_out));  // open: ovf
  Register #(.Bits(16)) IR (.D(driver_3_out), .C(clk), .en(IR_IE), .Q({OPCODE, IR0, IR1, IR2, IR3}));
  assign driver_3_out = R1_OE ? driver_1_out : 16'bz;  // Driver driver_3
  assign driver_3_out = R2_OE ? Register_file_db : 16'bz;  // Driver driver_4
  atk16_alu ALU (.A(driver_1_out), .B(Register_file_db), .S({OP_PARITY, IR3}), .Y(ALU_y), .FLAGS(ALU_flags));
  assign driver_3_out = PC_OE ? PC_out : 16'bz;  // Driver driver_5
  BitSelector #(.Selector_Bits(4)) bitselector_1 (.in({OPCODE, IR0, IR1, IR2, IR3}), .sel(4'b1111), .out(OP_PARITY));
  assign driver_3_out = ALU_OE ? ALU_y : 16'bz;  // Driver driver_6
  Register #(.Bits(4)) FR (.D(ALU_flags), .C(clk), .en(FR_IE), .Q(FR_q));
  not not_1 (not_1_out, clk);
  and and_1 (and_1_out, not_1_out, US_RS);
  Register #(.Bits(16)) MAR (.D(driver_3_out), .C(clk), .en(MAR_IE), .Q(MAR_q));
  BitSelector #(.Selector_Bits(2)) bitselector_2 (.in(FR_q), .sel(IR0[1:0]), .out(bitselector_2_out[3]));
  Demultiplexer #(.Bits(15)) demultiplexer_1 (
    .sel(MAR_q[15]), .in(MAR_q[14:0]), .out_0(demultiplexer_1_out_0), .out_1(demultiplexer_1_out_1));
  Counter #(.Bits(3)) Microsequencer (
    .en(1'b1), .C(not_1_out), .clr(and_1_out), .out(bitselector_2_out[2:0]));  // open: ovf
  EEPROM #(.AddrBits(8), .Bits(16), .isProgramMemory("true")) UCODE (
    .A({OPCODE, bitselector_2_out}), .CS(1'b1), .WE(1'b0), .OE(1'b1),
    .D({US_RS, HALT, FR_IE, ALU_OE, IR12_OE, IR9_OE, IR_IE, R2_OE, R1_OE, RW_IE, MEM_OE, MEM_IE, MAR_IE, PC_OE, PC_IE, PC_CO}));
  EEPROM #(.AddrBits(15), .Bits(16)) MEM_ROM (
    .A(demultiplexer_1_out_0), .CS(~MAR_q[15]), .WE(1'b0), .OE(MEM_OE), .D(MEM_ROM_d));
  RAMAsync #(.AddrBits(15), .Bits(16)) MEM_RAM (
    .A(demultiplexer_1_out_1), .D(driver_3_out), .we(MEM_IE), .Q(MEM_RAM_q));
  Driver #(.Bits(16)) driver_7 (.in(MEM_RAM_q), .en(MAR_q[15]));  // open: out
  assign driver_3_out = MEM_OE ? MEM_ROM_d : 16'bz;  // Driver driver_8

  // Other names for the same wires on the sheet: IR_L9[8:0] = {IR1, IR2, IR3}; IR_L12[11:0] = {IR0, IR1, IR2, IR3}
endmodule
